# Fritzing sketch ppdr-breadboard (saved by Fritzing 0.9.3b)

parts:
  Raspberry_Pi_1 = Raspberry Pi 3 [part_number=RPI-3-V1.2]
  Mod2 = L298N DC motor driver
  Mod3 = L298N DC motor driver
  M1 = DC Motor
  M2 = DC Motor
  M3 = DC Motor
  M4 = DC Motor
  Part1 = InvenSense MPU6050
  VCC1 = 4 x AAA Battery Mount
  U1 = TRANSCHIPTC5747 [package=camera_sfv24r-2st_2]  # not connected

nets:
  3V3: Raspberry_Pi_1.3v3, Part1.VCC
  N1: Raspberry_Pi_1.GPIO2, Part1.SDA
  N2: Raspberry_Pi_1.GPIO3, Part1.SCL
  GND: Raspberry_Pi_1.GND, Raspberry_Pi_1.GIPO22, Mod2.IN3, Part1.GND
  N3: Raspberry_Pi_1.GIPO17, Raspberry_Pi_1.GIPO15, Mod2.ENB
  N4: Raspberry_Pi_1.GIPO27, Raspberry_Pi_1.GIPO18, Mod2.IN4
  N5: Raspberry_Pi_1.GIPO10, Mod2.IN2
  N6: Raspberry_Pi_1.GIPO9, Mod2.IN1
  N7: Raspberry_Pi_1.GIPO11, Mod2.ENA
  N8: Raspberry_Pi_1.GIPO21, Mod3.ENB
  N9: Raspberry_Pi_1.GIPO20, Mod3.IN4
  N10: Raspberry_Pi_1.GIPO16, Mod3.IN3
  N11: Raspberry_Pi_1.GIPO25, Mod3.IN2
  N12: Raspberry_Pi_1.GIPO24, Mod3.IN1
  N13: Raspberry_Pi_1.GIPO23, Mod3.ENA
  N14: Mod2.OUT1, M2.pin_2
  N15: Mod2.OUT2, M2.pin_1
  N16: Mod2.OUT3, M4.pin_2
  N17: Mod2.OUT4, M4.pin_1
  N18: Mod3.OUT1, M3.pin_2
  N19: Mod3.OUT2, M3.pin_1
  N20: Mod3.12V, VCC1.+
  N21: Mod3.GND, VCC1.-
  N22: Mod3.OUT3, M1.pin_2
  N23: Mod3.OUT4, M1.pin_1

notes:
  Front Right Motor
  Front Left Motor
  Back Right Motor
  Back Left Motor
  Ribbon Cable
  Camera

custom parts:
  L298N DC motor driver: 2x DC motor driver with 78M05 positive voltage regulator (7..35 V) L298N: max 46 V, 2 A Set 5 V Enable jumper to enable 5 V regultor (needed for the L298N) and +5 V output at screw terminal or supply external +5 V at screw terminal Set ENA and/or ENB to +5 V to enable motor permanently or supply ENA and/or ENB with PWM signal IN1 and IN2 set rotation directory for motor A (OUT1/OUT2) IN2 and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
